// Logisim project PHANTOM_32.circ as structural Verilog
module alu (
  input  [3:0] op,
  input  [31:0] lhs,
  input  [31:0] rhs,
  output [31:0] result
);

  wire [0:0] comparator_1_lt, comparator_2_lt;
  wire [31:0] adder_1_out, and_1_out, nor_1_out, or_1_out, shifter_1_out, shifter_2_out, shifter_3_out,
       subtractor_1_out;

  Adder #(.width(32)) adder_1 (.a(lhs), .b(rhs), .out(adder_1_out), .cin(1'b0));  // open: cout
  Subtractor #(.width(32)) subtractor_1 (.a(lhs), .b(rhs), .out(subtractor_1_out), .bin(1'b0));  // open: bout
  assign and_1_out = lhs & rhs;  // AND_Gate and_1, 32 bits wide
  assign or_1_out = lhs | rhs;  // OR_Gate or_1, 32 bits wide
  assign nor_1_out = ~(lhs | rhs);  // NOR_Gate nor_1, 32 bits wide
  Shifter #(.width(32)) shifter_1 (.in(lhs), .\dist (rhs[4:0]), .out(shifter_1_out));
  Shifter #(.shift("lr"), .width(32)) shifter_2 (.in(lhs), .\dist (rhs[4:0]), .out(shifter_2_out));
  Shifter #(.shift("ar"), .width(32)) shifter_3 (.in(lhs), .\dist (rhs[4:0]), .out(shifter_3_out));
  Comparator #(.width(32)) comparator_1 (.a(lhs), .b(rhs), .lt(comparator_1_lt[0]));  // open: gt, eq
  Comparator #(.mode("unsigned"), .width(32)) comparator_2 (.a(lhs), .b(rhs), .lt(comparator_2_lt[0]));  // open: gt, eq
  Multiplexer #(.select(4), .width(32)) multiplexer_1 (
    .in0(adder_1_out), .in1(subtractor_1_out), .in2(and_1_out), .in3(or_1_out), .in4(nor_1_out),
    .in5(shifter_1_out), .in6(shifter_2_out), .in7(shifter_3_out), .in8({{31{1'b0}}, comparator_1_lt[0]}),
    .in9({{31{1'b0}}, comparator_2_lt[0]}), .in10(rhs), .in11(32'hdeadbeef), .in12(32'hdeadbeef),
    .in13(32'hdeadbeef), .in14(32'hdeadbeef), .in15(32'hdeadbeef), .out(result));  // open: sel
endmodule

module regfile (
  input  [4:0] rd_index_b,
  input  [4:0] rd_index_a,
  input  [4:0] wr_index,
  input  [31:0] wr_data,
  input  wr_en,
  input  clk,
  output [31:0] rd_data_b,
  output [31:0] rd_data_a
);

  wire and_2_out, and_3_out, and_4_out, and_5_out, and_6_out, and_7_out, and_8_out, and_9_out, and_10_out,
       and_11_out, and_12_out, and_13_out, and_14_out, and_15_out, and_16_out, and_17_out, and_18_out,
       and_19_out, and_20_out, and_21_out, and_22_out, and_23_out, and_24_out, and_25_out, and_26_out,
       and_27_out, and_28_out, and_29_out, and_30_out, and_31_out, and_32_out;
  wire [31:0] decoder_1_out0, register_1_q, register_2_q, register_3_q, register_4_q, register_5_q,
       register_6_q, register_7_q, register_8_q, register_9_q, register_10_q, register_11_q, register_12_q,
       register_13_q, register_14_q, register_15_q, register_16_q, register_17_q, register_18_q,
       register_19_q, register_20_q, register_21_q, register_22_q, register_23_q, register_24_q,
       register_25_q, register_26_q, register_27_q, register_28_q, register_29_q, register_30_q,
       register_31_q, register_32_q;

  Decoder #(.enable("false"), .select(5)) decoder_1 (
    .out0(decoder_1_out0[0]), .out1(decoder_1_out0[1]), .out2(decoder_1_out0[2]), .out3(decoder_1_out0[3]),
    .out4(decoder_1_out0[4]), .out5(decoder_1_out0[5]), .out6(decoder_1_out0[6]), .out7(decoder_1_out0[7]),
    .out8(decoder_1_out0[8]), .out9(decoder_1_out0[9]), .out10(decoder_1_out0[10]),
    .out11(decoder_1_out0[11]), .out12(decoder_1_out0[12]), .out13(decoder_1_out0[13]),
    .out14(decoder_1_out0[14]), .out15(decoder_1_out0[15]), .out16(decoder_1_out0[16]),
    .out17(decoder_1_out0[17]), .out18(decoder_1_out0[18]), .out19(decoder_1_out0[19]),
    .out20(decoder_1_out0[20]), .out21(decoder_1_out0[21]), .out22(decoder_1_out0[22]),
    .out23(decoder_1_out0[23]), .out24(decoder_1_out0[24]), .out25(decoder_1_out0[25]),
    .out26(decoder_1_out0[26]), .out27(decoder_1_out0[27]), .out28(decoder_1_out0[28]),
    .out29(decoder_1_out0[29]), .out30(decoder_1_out0[30]), .out31(decoder_1_out0[31]), .sel(wr_index));
  Register #(.width(32)) register_1 (.D(wr_data), .clk(clk), .Q(register_1_q), .clr(1'b0));  // open: en
  // AND_Gate and_1 has open pins: in0=decoder_1_out0[0], in1=wr_en, out=open
  Register #(.width(32)) register_2 (.D(wr_data), .en(and_2_out), .clk(clk), .Q(register_2_q), .clr(1'b0));
  and and_2 (and_2_out, decoder_1_out0[1], wr_en);
  Register #(.width(32)) register_3 (.D(wr_data), .en(and_3_out), .clk(clk), .Q(register_3_q), .clr(1'b0));
  and and_3 (and_3_out, decoder_1_out0[2], wr_en);
  Register #(.width(32)) register_4 (.D(wr_data), .en(and_4_out), .clk(clk), .Q(register_4_q), .clr(1'b0));
  and and_4 (and_4_out, decoder_1_out0[3], wr_en);
  Register #(.width(32)) register_5 (.D(wr_data), .en(and_5_out), .clk(clk), .Q(register_5_q), .clr(1'b0));
  and and_5 (and_5_out, decoder_1_out0[4], wr_en);
  Register #(.width(32)) register_6 (.D(wr_data), .en(and_6_out), .clk(clk), .Q(register_6_q), .clr(1'b0));
  and and_6 (and_6_out, decoder_1_out0[5], wr_en);
  Register #(.width(32)) register_7 (.D(wr_data), .en(and_7_out), .clk(clk), .Q(register_7_q), .clr(1'b0));
  and and_7 (and_7_out, decoder_1_out0[6], wr_en);
  Register #(.width(32)) register_8 (.D(wr_data), .en(and_8_out), .clk(clk), .Q(register_8_q), .clr(1'b0));
  and and_8 (and_8_out, decoder_1_out0[7], wr_en);
  Register #(.width(32)) register_9 (.D(wr_data), .en(and_9_out), .clk(clk), .Q(register_9_q), .clr(1'b0));
  and and_9 (and_9_out, decoder_1_out0[8], wr_en);
  Register #(.width(32)) register_10 (.D(wr_data), .en(and_10_out), .clk(clk), .Q(register_10_q), .clr(1'b0));
  and and_10 (and_10_out, decoder_1_out0[9], wr_en);
  Register #(.width(32)) register_11 (.D(wr_data), .en(and_11_out), .clk(clk), .Q(register_11_q), .clr(1'b0));
  and and_11 (and_11_out, decoder_1_out0[10], wr_en);
  Register #(.width(32)) register_12 (.D(wr_data), .en(and_12_out), .clk(clk), .Q(register_12_q), .clr(1'b0));
  and and_12 (and_12_out, decoder_1_out0[11], wr_en);
  Register #(.width(32)) register_13 (.D(wr_data), .en(and_13_out), .clk(clk), .Q(register_13_q), .clr(1'b0));
  and and_13 (and_13_out, decoder_1_out0[12], wr_en);
  Register #(.width(32)) register_14 (.D(wr_data), .en(and_14_out), .clk(clk), .Q(register_14_q), .clr(1'b0));
  and and_14 (and_14_out, decoder_1_out0[13], wr_en);
  Register #(.width(32)) register_15 (.D(wr_data), .en(and_15_out), .clk(clk), .Q(register_15_q), .clr(1'b0));
  and and_15 (and_15_out, decoder_1_out0[14], wr_en);
  Register #(.width(32)) register_16 (.D(wr_data), .en(and_16_out), .clk(clk), .Q(register_16_q), .clr(1'b0));
  and and_16 (and_16_out, decoder_1_out0[15], wr_en);
  Register #(.width(32)) register_17 (.D(wr_data), .en(and_17_out), .clk(clk), .Q(register_17_q), .clr(1'b0));
  and and_17 (and_17_out, decoder_1_out0[16], wr_en);
  Register #(.width(32)) register_18 (.D(wr_data), .en(and_18_out), .clk(clk), .Q(register_18_q), .clr(1'b0));
  and and_18 (and_18_out, decoder_1_out0[17], wr_en);
  Register #(.width(32)) register_19 (.D(wr_data), .en(and_19_out), .clk(clk), .Q(register_19_q), .clr(1'b0));
  and and_19 (and_19_out, decoder_1_out0[18], wr_en);
  Register #(.width(32)) register_20 (.D(wr_data), .en(and_20_out), .clk(clk), .Q(register_20_q), .clr(1'b0));
  and and_20 (and_20_out, decoder_1_out0[19], wr_en);
  Register #(.width(32)) register_21 (.D(wr_data), .en(and_21_out), .clk(clk), .Q(register_21_q), .clr(1'b0));
  and and_21 (and_21_out, decoder_1_out0[20], wr_en);
  Register #(.width(32)) register_22 (.D(wr_data), .en(and_22_out), .clk(clk), .Q(register_22_q), .clr(1'b0));
  and and_22 (and_22_out, decoder_1_out0[21], wr_en);
  Register #(.width(32)) register_23 (.D(wr_data), .en(and_23_out), .clk(clk), .Q(register_23_q), .clr(1'b0));
  and and_23 (and_23_out, decoder_1_out0[22], wr_en);
  Register #(.width(32)) register_24 (.D(wr_data), .en(and_24_out), .clk(clk), .Q(register_24_q), .clr(1'b0));
  and and_24 (and_24_out, decoder_1_out0[23], wr_en);
  Register #(.width(32)) register_25 (.D(wr_data), .en(and_25_out), .clk(clk), .Q(register_25_q), .clr(1'b0));
  and and_25 (and_25_out, decoder_1_out0[24], wr_en);
  Register #(.width(32)) register_26 (.D(wr_data), .en(and_26_out), .clk(clk), .Q(register_26_q), .clr(1'b0));
  and and_26 (and_26_out, decoder_1_out0[25], wr_en);
  Register #(.width(32)) register_27 (.D(wr_data), .en(and_27_out), .clk(clk), .Q(register_27_q), .clr(1'b0));
  and and_27 (and_27_out, decoder_1_out0[26], wr_en);
  Register #(.width(32)) register_28 (.D(wr_data), .en(and_28_out), .clk(clk), .Q(register_28_q), .clr(1'b0));
  and and_28 (and_28_out, decoder_1_out0[27], wr_en);
  Register #(.width(32)) register_29 (.D(wr_data), .en(and_29_out), .clk(clk), .Q(register_29_q), .clr(1'b0));
  and and_29 (and_29_out, decoder_1_out0[28], wr_en);
  Register #(.width(32)) register_30 (.D(wr_data), .en(and_30_out), .clk(clk), .Q(register_30_q), .clr(1'b0));
  and and_30 (and_30_out, decoder_1_out0[29], wr_en);
  Register #(.width(32)) register_31 (.D(wr_data), .en(and_31_out), .clk(clk), .Q(register_31_q), .clr(1'b0));
  and and_31 (and_31_out, decoder_1_out0[30], wr_en);
  Register #(.width(32)) register_32 (.D(wr_data), .en(and_32_out), .clk(clk), .Q(register_32_q), .clr(1'b0));
  and and_32 (and_32_out, decoder_1_out0[31], wr_en);
  Multiplexer #(.select(5), .width(32)) multiplexer_1 (
    .in0({32{1'b0}}), .in1(register_2_q), .in2(register_3_q), .in3(register_4_q), .in4(register_5_q),
    .in5(register_6_q), .in6(register_7_q), .in7(register_8_q), .in8(register_9_q), .in9(register_10_q),
    .in10(register_11_q), .in11(register_12_q), .in12(register_13_q), .in13(register_14_q),
    .in14(register_15_q), .in15(register_16_q), .in16(register_17_q), .in17(register_18_q),
    .in18(register_19_q), .in19(register_20_q), .in20(register_21_q), .in21(register_22_q),
    .in22(register_23_q), .in23(register_24_q), .in24(register_25_q), .in25(register_26_q),
    .in26(register_27_q), .in27(register_28_q), .in28(register_29_q), .in29(register_30_q),
    .in30(register_31_q), .in31(register_32_q), .out(rd_data_b), .sel(rd_index_b));
  Multiplexer #(.select(5), .width(32)) multiplexer_2 (
    .in0({32{1'b0}}), .in1(register_2_q), .in2(register_3_q), .in3(register_4_q), .in4(register_5_q),
    .in5(register_6_q), .in6(register_7_q), .in7(register_8_q), .in8(register_9_q), .in9(register_10_q),
    .in10(register_11_q), .in11(register_12_q), .in12(register_13_q), .in13(register_14_q),
    .in14(register_15_q), .in15(register_16_q), .in16(register_17_q), .in17(register_18_q),
    .in18(register_19_q), .in19(register_20_q), .in20(register_21_q), .in21(register_22_q),
    .in22(register_23_q), .in23(register_24_q), .in24(register_25_q), .in25(register_26_q),
    .in26(register_27_q), .in27(register_28_q), .in28(register_29_q), .in29(register_30_q),
    .in30(register_31_q), .in31(register_32_q), .out(rd_data_a), .sel(rd_index_a));
endmodule

module csr_regfile (
  input  [31:0] trap_mepc,
  input  [31:0] trap_mcause,
  input  [31:0] trap_mtval,
  input  [31:0] wr_data,
  input  [11:0] rd_addr,
  input  wr_en,
  input  mret_en,
  input  trap_en,
  input  resetn,
  input  [11:0] wr_addr,
  input  clk,
  output [31:0] out_mstatus,
  output [31:0] out_mtvec,
  output [31:0] out_mepc,
  output [31:0] rd_data
);

  wire and_5_out, and_6_out, and_8_out, and_10_out, and_12_out, and_15_out, and_19_out, and_21_out,
       comparator_2_eq, comparator_4_eq, comparator_6_eq, comparator_8_eq, comparator_10_eq,
       comparator_12_eq, comparator_14_eq, comparator_16_eq, comparator_17_eq, comparator_18_eq,
       comparator_19_eq, comparator_20_eq, comparator_21_eq, multiplexer_4_out, multiplexer_5_out,
       multiplexer_9_out, multiplexer_12_out, multiplexer_16_out, multiplexer_17_out, multiplexer_21_out,
       multiplexer_24_out, priority_encoder_1_en_out, priority_encoder_1_gs;
  wire [1:0] multiplexer_1_out, priority_encoder_1_out;
  wire [1:1] comparator_1_eq, comparator_3_eq, comparator_5_eq, comparator_7_eq, comparator_9_eq,
       comparator_11_eq, comparator_13_eq, comparator_15_eq;
  wire [31:0] and_1_out, and_2_out, and_3_out, and_4_out, and_7_out, and_9_out, and_11_out, and_13_out,
       and_14_out, and_16_out, and_17_out, and_18_out, and_20_out, MIE_out, MSTATUS_out, multiplexer_2_out,
       multiplexer_3_out, multiplexer_6_out, multiplexer_7_out, multiplexer_8_out, multiplexer_10_out,
       multiplexer_11_out, multiplexer_13_out, multiplexer_14_out, multiplexer_15_out, multiplexer_18_out,
       multiplexer_19_out, multiplexer_20_out, multiplexer_22_out, multiplexer_23_out, multiplexer_25_out,
       multiplexer_26_out, multiplexer_27_out, multiplexer_28_out, multiplexer_29_out, multiplexer_30_out,
       or_1_out, or_2_out, r_mcause_q, r_mie_q, r_mip_q, r_mscratch_q, r_mtval_q;

  Multiplexer #(.width(2)) multiplexer_1 (
    .in0(priority_encoder_1_out), .in1(2'b00), .out(multiplexer_1_out), .sel(priority_encoder_1_en_out));
  Priority_Encoder #(.select(2)) priority_encoder_1 (
    .in0(wr_en), .in1(mret_en), .in2(trap_en), .in3(resetn), .out(priority_encoder_1_out),
    .gs(priority_encoder_1_gs), .en_out(priority_encoder_1_en_out), .en_in(1'b1));
  assign MSTATUS_out = out_mstatus & 32'hffffe777;  // AND_Gate MSTATUS, 32 bits wide
  assign and_1_out = out_mstatus & 32'h8;  // AND_Gate and_1, 32 bits wide
  assign and_2_out = out_mstatus & 32'hffffe777;  // AND_Gate and_2, 32 bits wide
  assign and_3_out = out_mstatus & 32'h80;  // AND_Gate and_3, 32 bits wide
  assign and_4_out = wr_data & 32'h1888;  // AND_Gate and_4, 32 bits wide
  Comparator #(.mode("unsigned"), .width(12)) comparator_1 (
    .a(12'h300), .b(rd_addr), .eq(comparator_1_eq[1]));  // open: gt, lt
  and and_5 (and_5_out, priority_encoder_1_gs, ~multiplexer_1_out[1], ~multiplexer_1_out[0]);  // AND_Gate
  Comparator #(.mode("unsigned"), .width(12)) comparator_2 (
    .a(wr_addr), .b(12'h300), .eq(comparator_2_eq));  // open: gt, lt
  assign or_1_out = MSTATUS_out | {4'b0000, and_1_out[31:4]} | 32'h1800;  // OR_Gate or_1, 32 bits wide
  assign or_2_out = and_2_out | {4'b0000, and_3_out[31:4]} | 32'h1800;  // OR_Gate or_2, 32 bits wide
  Multiplexer #(.select(2), .width(32)) multiplexer_2 (
    .in0({32{1'b0}}), .in1({32{1'b0}}), .in2(out_mstatus), .in3(and_4_out), .out(multiplexer_2_out),
    .sel({comparator_1_eq[1], wr_en}));
  Multiplexer #(.select(2), .width(32)) multiplexer_3 (
    .in0(and_4_out), .in1(or_2_out), .in2(or_1_out), .in3(32'h1800), .out(multiplexer_3_out),
    .sel(multiplexer_1_out));
  Register #(.width(32)) r_mstatus (
    .D(multiplexer_3_out), .en(multiplexer_4_out), .clk(clk), .Q(out_mstatus), .clr(1'b0));
  Multiplexer multiplexer_4 (
    .in0(priority_encoder_1_gs), .in1(comparator_2_eq), .out(multiplexer_4_out), .sel(and_5_out));
  assign MIE_out = wr_data & 32'h888;  // AND_Gate MIE, 32 bits wide
  Comparator #(.mode("unsigned"), .width(12)) comparator_3 (
    .a(12'h304), .b(rd_addr), .eq(comparator_3_eq[1]));  // open: gt, lt
  and and_6 (and_6_out, priority_encoder_1_gs, ~multiplexer_1_out[1], ~multiplexer_1_out[0]);  // AND_Gate
  Multiplexer multiplexer_5 (
    .in0(priority_encoder_1_gs), .in1(comparator_4_eq), .out(multiplexer_5_out), .sel(and_6_out));
  Comparator #(.mode("unsigned"), .width(12)) comparator_4 (
    .a(wr_addr), .b(12'h304), .eq(comparator_4_eq));  // open: gt, lt
  Multiplexer #(.select(2), .width(32)) multiplexer_6 (
    .in0({32{1'b0}}), .in1({32{1'b0}}), .in2(r_mie_q), .in3(MIE_out), .out(multiplexer_6_out),
    .sel({comparator_3_eq[1], wr_en}));
  Multiplexer #(.select(2), .width(32)) multiplexer_7 (
    .in0(MIE_out), .in1(r_mie_q), .in2(r_mie_q), .in3({32{1'b0}}), .out(multiplexer_7_out),
    .sel(multiplexer_1_out));
  Register #(.width(32)) r_mie (.D(multiplexer_7_out), .en(multiplexer_5_out), .clk(clk), .Q(r_mie_q), .clr(1'b0));
  assign and_7_out = wr_data & 32'hfffffffd;  // AND_Gate and_7, 32 bits wide
  Comparator #(.mode("unsigned"), .width(12)) comparator_5 (
    .a(12'h305), .b(rd_addr), .eq(comparator_5_eq[1]));  // open: gt, lt
  Multiplexer #(.select(2), .width(32)) multiplexer_8 (
    .in0({32{1'b0}}), .in1({32{1'b0}}), .in2(out_mtvec), .in3(and_7_out), .out(multiplexer_8_out),
    .sel({comparator_5_eq[1], wr_en}));
  Register #(.width(32)) r_mtvec (.D(multiplexer_10_out), .en(multiplexer_9_out), .clk(clk), .Q(out_mtvec), .clr(1'b0));
  and and_8 (and_8_out, priority_encoder_1_gs, ~multiplexer_1_out[1], ~multiplexer_1_out[0]);  // AND_Gate
  Multiplexer multiplexer_9 (
    .in0(priority_encoder_1_gs), .in1(comparator_6_eq), .out(multiplexer_9_out), .sel(and_8_out));
  Comparator #(.mode("unsigned"), .width(12)) comparator_6 (
    .a(wr_addr), .b(12'h305), .eq(comparator_6_eq));  // open: gt, lt
  Multiplexer #(.select(2), .width(32)) multiplexer_10 (
    .in0(and_7_out), .in1(out_mtvec), .in2(out_mtvec), .in3({32{1'b0}}), .out(multiplexer_10_out),
    .sel(multiplexer_1_out));
  assign and_9_out = wr_data & {32{1'b1}};  // AND_Gate and_9, 32 bits wide
  Comparator #(.mode("unsigned"), .width(12)) comparator_7 (
    .a(12'h340), .b(rd_addr), .eq(comparator_7_eq[1]));  // open: gt, lt
  Comparator #(.mode("unsigned"), .width(12)) comparator_8 (
    .a(wr_addr), .b(12'h340), .eq(comparator_8_eq));  // open: gt, lt
  Multiplexer #(.select(2), .width(32)) multiplexer_11 (
    .in0({32{1'b0}}), .in1({32{1'b0}}), .in2(r_mscratch_q), .in3(and_9_out), .out(multiplexer_11_out),
    .sel({comparator_7_eq[1], wr_en}));
  Register #(.width(32)) r_mscratch (
    .D(multiplexer_13_out), .en(multiplexer_12_out), .clk(clk), .Q(r_mscratch_q), .clr(1'b0));
  and and_10 (and_10_out, priority_encoder_1_gs, ~multiplexer_1_out[1], ~multiplexer_1_out[0]);  // AND_Gate
  Multiplexer multiplexer_12 (
    .in0(priority_encoder_1_gs), .in1(comparator_8_eq), .out(multiplexer_12_out), .sel(and_10_out));
  Multiplexer #(.select(2), .width(32)) multiplexer_13 (
    .in0(and_9_out), .in1(r_mscratch_q), .in2(r_mscratch_q), .in3({32{1'b0}}), .out(multiplexer_13_out),
    .sel(multiplexer_1_out));
  assign and_11_out = wr_data & 32'hfffffffe;  // AND_Gate and_11, 32 bits wide
  Comparator #(.mode("unsigned"), .width(12)) comparator_9 (
    .a(12'h341), .b(rd_addr), .eq(comparator_9_eq[1]));  // open: gt, lt
  and and_12 (and_12_out, priority_encoder_1_gs, ~multiplexer_1_out[1], ~multiplexer_1_out[0]);  // AND_Gate
  Comparator #(.mode("unsigned"), .width(12)) comparator_10 (
    .a(wr_addr), .b(12'h341), .eq(comparator_10_eq));  // open: gt, lt
  assign and_13_out = trap_mepc & 32'hfffffffe;  // AND_Gate and_13, 32 bits wide
  Multiplexer #(.select(2), .width(32)) multiplexer_14 (
    .in0({32{1'b0}}), .in1({32{1'b0}}), .in2(out_mepc), .in3(and_11_out), .out(multiplexer_14_out),
    .sel({comparator_9_eq[1], wr_en}));
  Multiplexer #(.select(2), .width(32)) multiplexer_15 (
    .in0(and_11_out), .in1(out_mepc), .in2(and_13_out), .in3({32{1'b0}}), .out(multiplexer_15_out),
    .sel(multiplexer_1_out));
  Register #(.width(32)) r_mepc (.D(multiplexer_15_out), .en(multiplexer_16_out), .clk(clk), .Q(out_mepc), .clr(1'b0));
  Multiplexer multiplexer_16 (
    .in0(priority_encoder_1_gs), .in1(comparator_10_eq), .out(multiplexer_16_out), .sel(and_12_out));
  assign and_14_out = wr_data & 32'h8000000f;  // AND_Gate and_14, 32 bits wide
  Comparator #(.mode("unsigned"), .width(12)) comparator_11 (
    .a(12'h342), .b(rd_addr), .eq(comparator_11_eq[1]));  // open: gt, lt
  and and_15 (and_15_out, priority_encoder_1_gs, ~multiplexer_1_out[1], ~multiplexer_1_out[0]);  // AND_Gate
  Multiplexer multiplexer_17 (
    .in0(priority_encoder_1_gs), .in1(comparator_12_eq), .out(multiplexer_17_out), .sel(and_15_out));
  Comparator #(.mode("unsigned"), .width(12)) comparator_12 (
    .a(wr_addr), .b(12'h342), .eq(comparator_12_eq));  // open: gt, lt
  assign and_16_out = trap_mcause & 32'h8000000f;  // AND_Gate and_16, 32 bits wide
  Multiplexer #(.select(2), .width(32)) multiplexer_18 (
    .in0({32{1'b0}}), .in1({32{1'b0}}), .in2(r_mcause_q), .in3(and_14_out), .out(multiplexer_18_out),
    .sel({comparator_11_eq[1], wr_en}));
  Multiplexer #(.select(2), .width(32)) multiplexer_19 (
    .in0(and_14_out), .in1(r_mcause_q), .in2(and_16_out), .in3({32{1'b0}}), .out(multiplexer_19_out),
    .sel(multiplexer_1_out));
  Register #(.width(32)) r_mcause (
    .D(multiplexer_19_out), .en(multiplexer_17_out), .clk(clk), .Q(r_mcause_q), .clr(1'b0));
  assign and_17_out = wr_data & {32{1'b1}};  // AND_Gate and_17, 32 bits wide
  Comparator #(.mode("unsigned"), .width(12)) comparator_13 (
    .a(12'h343), .b(rd_addr), .eq(comparator_13_eq[1]));  // open: gt, lt
  assign and_18_out = trap_mtval & {32{1'b1}};  // AND_Gate and_18, 32 bits wide
  Multiplexer #(.select(2), .width(32)) multiplexer_20 (
    .in0({32{1'b0}}), .in1({32{1'b0}}), .in2(r_mtval_q), .in3(and_17_out), .out(multiplexer_20_out),
    .sel({comparator_13_eq[1], wr_en}));
  Register #(.width(32)) r_mtval (
    .D(multiplexer_22_out), .en(multiplexer_21_out), .clk(clk), .Q(r_mtval_q), .clr(1'b0));
  and and_19 (and_19_out, priority_encoder_1_gs, ~multiplexer_1_out[1], ~multiplexer_1_out[0]);  // AND_Gate
  Multiplexer multiplexer_21 (
    .in0(priority_encoder_1_gs), .in1(comparator_14_eq), .out(multiplexer_21_out), .sel(and_19_out));
  Comparator #(.mode("unsigned"), .width(12)) comparator_14 (
    .a(wr_addr), .b(12'h343), .eq(comparator_14_eq));  // open: gt, lt
  Multiplexer #(.select(2), .width(32)) multiplexer_22 (
    .in0(and_17_out), .in1(r_mtval_q), .in2(and_18_out), .in3({32{1'b0}}), .out(multiplexer_22_out),
    .sel(multiplexer_1_out));
  assign and_20_out = wr_data & 32'h888;  // AND_Gate and_20, 32 bits wide
  Comparator #(.mode("unsigned"), .width(12)) comparator_15 (
    .a(12'h344), .b(rd_addr), .eq(comparator_15_eq[1]));  // open: gt, lt
  Comparator #(.mode("unsigned"), .width(12)) comparator_16 (
    .a(wr_addr), .b(12'h344), .eq(comparator_16_eq));  // open: gt, lt
  Multiplexer #(.select(2), .width(32)) multiplexer_23 (
    .in0({32{1'b0}}), .in1({32{1'b0}}), .in2(r_mip_q), .in3(and_20_out), .out(multiplexer_23_out),
    .sel({comparator_15_eq[1], wr_en}));
  Register #(.width(32)) r_mip (.D(multiplexer_25_out), .en(multiplexer_24_out), .clk(clk), .Q(r_mip_q), .clr(1'b0));
  and and_21 (and_21_out, priority_encoder_1_gs, ~multiplexer_1_out[1], ~multiplexer_1_out[0]);  // AND_Gate
  Multiplexer multiplexer_24 (
    .in0(priority_encoder_1_gs), .in1(comparator_16_eq), .out(multiplexer_24_out), .sel(and_21_out));
  Multiplexer #(.select(2), .width(32)) multiplexer_25 (
    .in0(and_20_out), .in1(r_mip_q), .in2(r_mip_q), .in3({32{1'b0}}), .out(multiplexer_25_out),
    .sel(multiplexer_1_out));
  Comparator #(.mode("unsigned"), .width(12)) comparator_17 (
    .a(12'h301), .b(rd_addr), .eq(comparator_17_eq));  // open: gt, lt
  Multiplexer #(.width(32)) multiplexer_26 (
    .in0({32{1'b0}}), .in1(32'h40000104), .out(multiplexer_26_out), .sel(comparator_17_eq));
  Multiplexer #(.width(32)) multiplexer_27 (
    .in0({32{1'b0}}), .in1({32{1'b0}}), .out(multiplexer_27_out), .sel(comparator_18_eq));
  Comparator #(.mode("unsigned"), .width(12)) comparator_18 (
    .a(12'hf11), .b(rd_addr), .eq(comparator_18_eq));  // open: gt, lt
  Multiplexer #(.width(32)) multiplexer_28 (
    .in0({32{1'b0}}), .in1({32{1'b0}}), .out(multiplexer_28_out), .sel(comparator_19_eq));
  Comparator #(.mode("unsigned"), .width(12)) comparator_19 (
    .a(12'hf12), .b(rd_addr), .eq(comparator_19_eq));  // open: gt, lt
  Comparator #(.mode("unsigned"), .width(12)) comparator_20 (
    .a(12'hf13), .b(rd_addr), .eq(comparator_20_eq));  // open: gt, lt
  Multiplexer #(.width(32)) multiplexer_29 (
    .in0({32{1'b0}}), .in1(32'h1), .out(multiplexer_29_out), .sel(comparator_20_eq));
  Multiplexer #(.width(32)) multiplexer_30 (
    .in0({32{1'b0}}), .in1({32{1'b0}}), .out(multiplexer_30_out), .sel(comparator_21_eq));
  Comparator #(.mode("unsigned"), .width(12)) comparator_21 (
    .a(12'hf14), .b(rd_addr), .eq(comparator_21_eq));  // open: gt, lt
  assign rd_data = multiplexer_30_out | multiplexer_29_out | multiplexer_28_out | multiplexer_27_out | multiplexer_26_out | multiplexer_23_out | multiplexer_20_out | multiplexer_18_out | multiplexer_14_out | multiplexer_11_out | multiplexer_8_out | multiplexer_6_out | multiplexer_2_out;  // OR_Gate or_3, 32 bits wide
endmodule

module imm_generator (
  input  [31:0] instrWord,
  output [31:0] immediate,
  output [31:0] immediate2
);

  wire comparator_1_eq, comparator_2_eq, comparator_3_eq, comparator_4_eq, comparator_5_eq, comparator_6_eq,
       comparator_7_eq, comparator_10_eq;
  wire [1:0] comparator_9_eq;
  wire [31:0] immShamt, multiplexer_1_out, multiplexer_2_out, multiplexer_3_out, multiplexer_4_out,
       multiplexer_5_out, multiplexer_6_out, multiplexer_7_out, multiplexer_8_out, multiplexer_9_out,
       multiplexer_10_out, multiplexer_11_out, multiplexer_12_out, multiplexer_13_out, or_1_out;
  wire [31:5] immCTypeLI;
  wire [31:8] immCTypeB;
  wire [31:9] immCType16SP;
  wire [31:11] immCTypeJ, immTypeI, immTypeS;
  wire [31:12] immTypeB;
  wire [31:17] immCTypeLUI;
  wire [31:20] immTypeJ;

  assign immTypeJ = {{11{instrWord[31]}}, instrWord[31]};  // Bit_Extender bit_extender_1
  assign immTypeS = {{20{instrWord[31]}}, instrWord[31]};  // Bit_Extender bit_extender_2
  assign immTypeB = {{19{instrWord[31]}}, instrWord[31]};  // Bit_Extender bit_extender_3
  assign immTypeI = {{20{instrWord[31]}}, instrWord[31]};  // Bit_Extender bit_extender_4
  assign immCTypeLUI = {{14{instrWord[12]}}, instrWord[12]};  // Bit_Extender bit_extender_5
  assign immCType16SP = {{22{instrWord[12]}}, instrWord[12]};  // Bit_Extender bit_extender_6
  assign immCTypeB = {{23{instrWord[12]}}, instrWord[12]};  // Bit_Extender bit_extender_7
  assign immCTypeJ = {{20{instrWord[12]}}, instrWord[12]};  // Bit_Extender bit_extender_8
  assign immCTypeLI = {{26{instrWord[12]}}, instrWord[12]};  // Bit_Extender bit_extender_9
  Comparator #(.width(7)) comparator_1 (.a(instrWord[6:0]), .b(7'b0110111), .eq(comparator_1_eq));  // open: gt, lt
  Comparator #(.width(7)) comparator_2 (.a(instrWord[6:0]), .b(7'b0010111), .eq(comparator_2_eq));  // open: gt, lt
  Comparator #(.width(7)) comparator_3 (.a(instrWord[6:0]), .b(7'b1101111), .eq(comparator_3_eq));  // open: gt, lt
  Comparator #(.width(7)) comparator_4 (.a(instrWord[6:0]), .b(7'b1100111), .eq(comparator_4_eq));  // open: gt, lt
  Comparator #(.width(7)) comparator_5 (.a(instrWord[6:0]), .b(7'b1100011), .eq(comparator_5_eq));  // open: gt, lt
  Comparator #(.width(7)) comparator_6 (.a(instrWord[6:0]), .b(7'b0000011), .eq(comparator_6_eq));  // open: gt, lt
  Comparator #(.width(7)) comparator_7 (.a(instrWord[6:0]), .b(7'b0100011), .eq(comparator_7_eq));  // open: gt, lt
  Comparator #(.width(7)) comparator_8 (.a(instrWord[6:0]), .b(7'b0010011), .eq(comparator_9_eq[1]));  // open: gt, lt
  Comparator #(.width(2)) comparator_9 (.a(instrWord[13:12]), .b(2'b01), .eq(comparator_9_eq[0]));  // open: gt, lt
  Multiplexer #(.width(32)) multiplexer_1 (
    .in0({32{1'b0}}), .in1({instrWord[31:12], {12{1'b0}}}), .out(multiplexer_1_out), .sel(comparator_1_eq));
  Multiplexer #(.width(32)) multiplexer_2 (
    .in0({32{1'b0}}), .in1({instrWord[31:12], {12{1'b0}}}), .out(multiplexer_2_out), .sel(comparator_2_eq));
  Multiplexer #(.width(32)) multiplexer_3 (
    .in0({32{1'b0}}), .in1({immTypeJ, instrWord[19:12], instrWord[20], instrWord[30:21], 1'b0}),
    .out(multiplexer_3_out), .sel(comparator_3_eq));
  Multiplexer #(.width(32)) multiplexer_4 (
    .in0({32{1'b0}}), .in1({immTypeI, instrWord[30:20]}), .out(multiplexer_4_out), .sel(comparator_4_eq));
  Multiplexer #(.width(32)) multiplexer_5 (
    .in0({32{1'b0}}), .in1({immTypeB, instrWord[7], instrWord[30:25], instrWord[11:8], 1'b0}),
    .out(multiplexer_5_out), .sel(comparator_5_eq));
  Multiplexer #(.width(32)) multiplexer_6 (
    .in0({32{1'b0}}), .in1({immTypeI, instrWord[30:20]}), .out(multiplexer_6_out), .sel(comparator_6_eq));
  Multiplexer #(.width(32)) multiplexer_7 (
    .in0({32{1'b0}}), .in1({immTypeS, instrWord[30:25], instrWord[11:7]}), .out(multiplexer_7_out),
    .sel(comparator_7_eq));
  Multiplexer #(.select(2), .width(32)) multiplexer_8 (
    .in0({32{1'b0}}), .in1({32{1'b0}}), .in2({immTypeI, instrWord[30:20]}), .in3(immShamt),
    .out(multiplexer_8_out), .sel(comparator_9_eq));
  assign or_1_out = multiplexer_1_out | multiplexer_2_out | multiplexer_3_out | multiplexer_4_out | multiplexer_5_out | multiplexer_6_out | multiplexer_7_out | multiplexer_8_out;  // OR_Gate or_1, 32 bits wide
  Comparator #(.width(5)) comparator_10 (.a(instrWord[11:7]), .b(5'b00010), .eq(comparator_10_eq));  // open: gt, lt
  Multiplexer #(.width(32)) multiplexer_9 (
    .in0({immCTypeLUI, instrWord[6:2], {12{1'b0}}}),
    .in1({immCType16SP, instrWord[4:3], instrWord[5], instrWord[2], instrWord[6], 4'b0000}),
    .out(multiplexer_9_out), .sel(comparator_10_eq));
  Multiplexer #(.select(2), .width(32)) multiplexer_10 (
    .in0({{27{1'b0}}, instrWord[6:2]}), .in1({{27{1'b0}}, instrWord[6:2]}),
    .in2({immCTypeLI, instrWord[6:2]}), .in3({32{1'b0}}), .out(multiplexer_10_out), .sel(instrWord[11:10]));
  Multiplexer #(.select(3), .width(32)) multiplexer_11 (
    .in0({{22{1'b0}}, instrWord[10:7], instrWord[12:11], instrWord[5], instrWord[6], 2'b00}),
    .in1({32{1'b0}}), .in2({{25{1'b0}}, instrWord[5], instrWord[12:10], instrWord[6], 2'b00}),
    .in3({32{1'b0}}), .in4({32{1'b0}}), .in5({32{1'b0}}),
    .in6({{25{1'b0}}, instrWord[5], instrWord[12:10], instrWord[6], 2'b00}), .in7({32{1'b0}}),
    .out(multiplexer_11_out));  // open: sel
  Multiplexer #(.select(3), .width(32)) multiplexer_12 (
    .in0({immCTypeLI, instrWord[6:2]}),
    .in1({immCTypeJ, instrWord[8], instrWord[10:9], instrWord[6], instrWord[7], instrWord[2], instrWord[11], instrWord[5:3], 1'b0}),
    .in2({immCTypeLI, instrWord[6:2]}), .in3(multiplexer_9_out), .in4(multiplexer_10_out),
    .in5({immCTypeJ, instrWord[8], instrWord[10:9], instrWord[6], instrWord[7], instrWord[2], instrWord[11], instrWord[5:3], 1'b0}),
    .in6({immCTypeB, instrWord[6:5], instrWord[2], instrWord[11:10], instrWord[4:3], 1'b0}),
    .in7({immCTypeB, instrWord[6:5], instrWord[2], instrWord[11:10], instrWord[4:3], 1'b0}),
    .out(multiplexer_12_out));  // open: sel
  Multiplexer #(.select(3), .width(32)) multiplexer_13 (
    .in0({{27{1'b0}}, instrWord[6:2]}), .in1({32{1'b0}}),
    .in2({{24{1'b0}}, instrWord[3:2], instrWord[12], instrWord[6:4], 2'b00}), .in3({32{1'b0}}),
    .in4({32{1'b0}}), .in5({32{1'b0}}), .in6({{24{1'b0}}, instrWord[8:7], instrWord[12:9], 2'b00}),
    .in7({32{1'b0}}), .out(multiplexer_13_out));  // open: sel
  Multiplexer #(.select(2), .width(32)) multiplexer_14 (
    .in0(multiplexer_11_out), .in1(multiplexer_12_out), .in2(multiplexer_13_out), .in3(or_1_out),
    .out(immediate));  // open: sel
  Adder #(.width(32)) adder_1 (.a(immediate), .b(32'h2), .out(immediate2), .cin(1'b0));  // open: cout

  // Other names for the same wires on the sheet: func3[2:0] = instrWord[14:12];
  //   immCType4SPN[9:2] = {instrWord[10:7], instrWord[12:11], instrWord[5], instrWord[6]};
  //   immCTypeLW[6:2] = {instrWord[5], instrWord[12:10], instrWord[6]};
  //   immCTypeLWSP[7:2] = {instrWord[3:2], instrWord[12], instrWord[6:4]};
  //   immCTypeSWSP[7:2] = {instrWord[8:7], instrWord[12:9]};
  //   immTypeJ[19:1] = {instrWord[19:12], instrWord[20], instrWord[30:21]}; immTypeU[31:12] = instrWord[31:12];
  //   immCType16SP[8:4] = {instrWord[4:3], instrWord[5], instrWord[2], instrWord[6]};
  //   immCTypeB[7:1] = {instrWord[6:5], instrWord[2], instrWord[11:10], instrWord[4:3]};
  //   immCTypeJ[10:1] = {instrWord[8], instrWord[10:9], instrWord[6], instrWord[7], instrWord[2], instrWord[11], instrWord[5:3]};
  //   immCTypeLI[4:0] = instrWord[6:2]; immCTypeLUI[16:12] = instrWord[6:2]; immCTypeSHMT[4:0] = instrWord[6:2];
  //   primaryOpcode[6:0] = instrWord[6:0]; compressedArithOp[1:0] = instrWord[11:10];
  //   compressedDestRegFull[4:0] = instrWord[11:7];
  //   immTypeB[11:1] = {instrWord[7], instrWord[30:25], instrWord[11:8]};
  //   immTypeS[10:0] = {instrWord[30:25], instrWord[11:7]}; immShamt32[4:0] = instrWord[24:20];
  //   immTypeI[10:0] = instrWord[30:20]; compressedFunc3[2:0] = instrWord[15:13];
  //   compressedQuadrant[1:0] = instrWord[1:0]
endmodule

module branch_eval (
  input  [31:0] rs1_data,
  input  [31:0] rs2_data,
  input  [2:0] branch_type,
  output branch_taken
);

  wire comparator_1_eq, comparator_2_eq, comparator_3_lt, comparator_4_eq, comparator_4_gt, comparator_5_lt,
       comparator_6_eq, comparator_6_gt, not_1_out, or_1_out, or_2_out;

  Comparator #(.mode("unsigned"), .width(32)) comparator_1 (
    .a(rs1_data), .b(rs2_data), .eq(comparator_1_eq));  // open: gt, lt
  Comparator #(.mode("unsigned"), .width(32)) comparator_2 (
    .a(rs1_data), .b(rs2_data), .eq(comparator_2_eq));  // open: gt, lt
  Comparator #(.width(32)) comparator_3 (.a(rs1_data), .b(rs2_data), .lt(comparator_3_lt));  // open: gt, eq
  Comparator #(.width(32)) comparator_4 (
    .a(rs1_data), .b(rs2_data), .gt(comparator_4_gt), .eq(comparator_4_eq));  // open: lt
  Comparator #(.mode("unsigned"), .width(32)) comparator_5 (
    .a(rs1_data), .b(rs2_data), .lt(comparator_5_lt));  // open: gt, eq
  Comparator #(.mode("unsigned"), .width(32)) comparator_6 (
    .a(rs1_data), .b(rs2_data), .gt(comparator_6_gt), .eq(comparator_6_eq));  // open: lt
  not not_1 (not_1_out, comparator_2_eq);
  or or_1 (or_1_out, comparator_4_gt, comparator_4_eq);
  or or_2 (or_2_out, comparator_6_gt, comparator_6_eq);
  Multiplexer #(.select(3)) multiplexer_1 (
    .in0(comparator_1_eq), .in1(not_1_out), .in2(1'b0), .in3(1'b0), .in4(comparator_3_lt), .in5(or_1_out),
    .in6(comparator_5_lt), .in7(or_2_out), .out(branch_taken), .sel(branch_type));
endmodule

module branch_target (
  input  [31:0] immediate,
  input  [31:0] rs1_data,
  input  is_jalr,
  input  [31:0] pc,
  input  [31:0] immediate_2,
  output [31:0] target_addr,
  output [31:0] target_addr_2
);

  wire [31:0] adder_1_out, adder_2_out, adder_3_out, adder_4_out, and_1_out, and_2_out, and_3_out, and_4_out;

  Adder #(.width(32)) adder_1 (.a(rs1_data), .b(immediate), .out(adder_1_out), .cin(1'b0));  // open: cout
  Adder #(.width(32)) adder_2 (.a(pc), .b(immediate), .out(adder_2_out), .cin(1'b0));  // open: cout
  Adder #(.width(32)) adder_3 (.a(rs1_data), .b(immediate_2), .out(adder_3_out), .cin(1'b0));  // open: cout
  Adder #(.width(32)) adder_4 (.a(pc), .b(immediate_2), .out(adder_4_out), .cin(1'b0));  // open: cout
  assign and_1_out = adder_1_out & 32'hfffffffe;  // AND_Gate and_1, 32 bits wide
  Multiplexer #(.width(32)) multiplexer_1 (.in0(and_1_out), .in1(and_2_out), .out(target_addr), .sel(is_jalr));
  assign and_2_out = {32{1'b1}} & adder_2_out;  // AND_Gate and_2, 32 bits wide
  assign and_3_out = adder_3_out & 32'hfffffffe;  // AND_Gate and_3, 32 bits wide
  Multiplexer #(.width(32)) multiplexer_2 (.in0(and_3_out), .in1(and_4_out), .out(target_addr_2), .sel(is_jalr));
  assign and_4_out = {32{1'b1}} & adder_4_out;  // AND_Gate and_4, 32 bits wide
endmodule

module forwarding_unit (
  input  [4:0] ex_rs1_index,
  input  [4:0] ex_rs2_index,
  input  [4:0] ma_rd_index,
  input  [1:0] fwd_A_sel,
  input  ma_reg_write,
  input  ma_rd_nonzero,
  input  [4:0] wb_rd_index,
  input  wb_reg_write,
  input  wb_rd_nonzero,
  input  [1:0] fwd_B_sel
);

  wire comparator_1_eq, comparator_2_eq, comparator_3_eq, comparator_4_eq;
  wire [1:0] and_2_out, and_4_out;

  Comparator #(.width(5)) comparator_1 (.a(ex_rs1_index), .b(ma_rd_index), .eq(comparator_1_eq));  // open: gt, lt
  Comparator #(.width(5)) comparator_2 (.a(ex_rs1_index), .b(wb_rd_index), .eq(comparator_2_eq));  // open: gt, lt
  Comparator #(.width(5)) comparator_3 (.a(ex_rs2_index), .b(ma_rd_index), .eq(comparator_3_eq));  // open: gt, lt
  Comparator #(.width(5)) comparator_4 (.a(ex_rs2_index), .b(wb_rd_index), .eq(comparator_4_eq));  // open: gt, lt
  and and_1 (and_2_out[1], ma_reg_write, ma_rd_nonzero, comparator_1_eq);
  and and_2 (and_2_out[0], wb_reg_write, wb_rd_nonzero, comparator_2_eq);
  and and_3 (and_4_out[1], ma_reg_write, ma_rd_nonzero, comparator_3_eq);
  and and_4 (and_4_out[0], wb_reg_write, wb_rd_nonzero, comparator_4_eq);
  Multiplexer #(.select(2), .width(2)) multiplexer_1 (
    .in0(2'b00), .in1(2'b01), .in2(2'b10), .in3(2'b10), .out(fwd_A_sel), .sel(and_2_out));
  Multiplexer #(.select(2), .width(2)) multiplexer_2 (
    .in0(2'b00), .in1(2'b01), .in2(2'b10), .in3(2'b10), .out(fwd_B_sel), .sel(and_4_out));
endmodule

module hazard_unit (
  input  id_is_load,
  input  [4:0] if_rs1_index,
  input  [4:0] if_rs2_index,
  input  [4:0] id_rd_index,
  output stall
);

  wire comparator_1_eq, comparator_2_eq, comparator_3_eq, or_1_out;

  Comparator #(.width(5)) comparator_1 (.a(if_rs1_index), .b(id_rd_index), .eq(comparator_1_eq));  // open: gt, lt
  Comparator #(.width(5)) comparator_2 (.a(id_rd_index), .b(if_rs2_index), .eq(comparator_2_eq));  // open: gt, lt
  or or_1 (or_1_out, comparator_1_eq, comparator_2_eq);
  Comparator #(.width(5)) comparator_3 (.a({5{1'b0}}), .b(id_rd_index), .eq(comparator_3_eq));  // open: gt, lt
  and and_1 (stall, id_is_load, or_1_out, comparator_3_eq);
endmodule

module branch_target_buffer (
  input  [31:0] next_pc,
  input  update_en,
  input  clk,
  input  [31:0] update_target,
  input  [8:0] update_idx,
  output [31:0] btb_rdata
);

  wire not_1_out;
  wire [8:0] btb_mar_q, multiplexer_1_out;

  Register #(.width(9)) btb_mar (.D(next_pc[9:1]), .en(clk), .clk(clk), .Q(btb_mar_q), .clr(1'b0));
  Multiplexer #(.width(9)) multiplexer_1 (.in0(btb_mar_q), .in1(update_idx), .out(multiplexer_1_out), .sel(clk));
  not not_1 (not_1_out, clk);
  RAM #(.addrWidth(9), .dataWidth(32), .enables("line")) Branch_Target_Buffer (
    .addr(multiplexer_1_out), .we(update_en), .clk(not_1_out), .din(update_target), .dout(btb_rdata));
endmodule

module pattern_history_table (
  input  clk,
  input  [12:0] r_bhr,
  input  [31:0] pre_pc,
  input  update_en,
  input  [12:0] update_idx,
  input  update_taken,
  input  [1:0] update_old,
  output [12:0] pht_mar,
  output [1:0] pht_rdata
);

  wire and_1_out, nor_1_out, not_1_out;
  wire [1:0] adder_1_out, multiplexer_1_out, multiplexer_2_out, multiplexer_4_out, subtractor_1_out;
  wire [12:0] multiplexer_3_out, xor_1_out;

  nor nor_1 (nor_1_out, update_old[0], update_old[1]);
  and and_1 (and_1_out, update_old[0], update_old[1]);
  Register #(.width(13)) r_pht_mar (.D(xor_1_out), .en(clk), .clk(clk), .Q(pht_mar), .clr(1'b0));
  assign xor_1_out = r_bhr ^ pre_pc[13:1];  // XOR_Gate xor_1, 13 bits wide
  Subtractor #(.width(2)) subtractor_1 (.a(update_old), .b(2'b01), .out(subtractor_1_out));  // open: bin, bout
  Adder #(.width(2)) adder_1 (.a(update_old), .b(2'b01), .out(adder_1_out), .cin(1'b0));  // open: cout
  Multiplexer #(.width(2)) multiplexer_1 (
    .in0(subtractor_1_out), .in1(2'b00), .out(multiplexer_1_out), .sel(nor_1_out));
  Multiplexer #(.width(2)) multiplexer_2 (.in0(adder_1_out), .in1(2'b11), .out(multiplexer_2_out), .sel(and_1_out));
  not not_1 (not_1_out, clk);
  Multiplexer #(.width(13)) multiplexer_3 (.in0(pht_mar), .in1(update_idx), .out(multiplexer_3_out), .sel(clk));
  Multiplexer #(.width(2)) multiplexer_4 (
    .in0(multiplexer_1_out), .in1(multiplexer_2_out), .out(multiplexer_4_out), .sel(update_taken));
  RAM #(.addrWidth(13), .dataWidth(2), .enables("line")) Pattern_History_Table (
    .addr(multiplexer_3_out), .we(update_en), .clk(not_1_out), .din(multiplexer_4_out), .dout(pht_rdata));
endmodule

module trap_unit (
  input  ma_mem_write,
  input  [2:0] ma_mem_width,
  input  ma_mem_read,
  input  ma_is_ecall,
  input  ma_is_ebreak,
  input  ma_is_illegal,
  input  ma_is_mret,
  input  [31:0] ma_dmemAddr,
  input  [31:0] ma_instr,
  input  [31:0] ma_pc,
  output trap_en,
  output mret_en,
  output [31:0] trap_mcause,
  output [31:0] trap_mtval,
  output [31:0] trap_mepc
);

  wire and_1_out, and_2_out, and_3_out, and_4_out, and_5_out, and_6_out, comparator_1_eq, comparator_2_eq,
       comparator_3_eq, comparator_4_eq, comparator_5_eq, nor_1_out, nor_2_out, or_1_out, or_2_out, or_3_out;
  wire [2:0] priority_encoder_1_out, priority_encoder_2_out;

  Comparator #(.width(3)) comparator_1 (.a(ma_mem_width), .b(3'b001), .eq(comparator_1_eq));  // open: gt, lt
  nor nor_1 (nor_1_out, ma_dmemAddr[0], ma_dmemAddr[1]);
  Comparator #(.width(3)) comparator_2 (.a(ma_mem_width), .b(3'b010), .eq(comparator_2_eq));  // open: gt, lt
  Comparator #(.width(3)) comparator_3 (.a(ma_mem_width), .b(3'b001), .eq(comparator_3_eq));  // open: gt, lt
  or or_1 (or_1_out, comparator_3_eq, comparator_4_eq);
  Comparator #(.width(3)) comparator_4 (.a(ma_mem_width), .b(3'b101), .eq(comparator_4_eq));  // open: gt, lt
  nor nor_2 (nor_2_out, ma_dmemAddr[0], ma_dmemAddr[1]);
  Comparator #(.width(3)) comparator_5 (.a(ma_mem_width), .b(3'b010), .eq(comparator_5_eq));  // open: gt, lt
  Priority_Encoder priority_encoder_1 (
    .in0(1'b1), .in1(1'b0), .in2(1'b0), .in3(and_5_out), .in4(and_6_out), .in5(ma_is_ecall),
    .in6(ma_is_illegal), .in7(ma_is_ebreak), .out(priority_encoder_1_out), .en_in(1'b1));  // open: gs, en_out
  Priority_Encoder priority_encoder_2 (
    .in0(1'b1), .in1(1'b0), .in2(1'b0), .in3(1'b0), .in4(and_5_out), .in5(and_6_out), .in6(ma_is_illegal),
    .in7(ma_is_ebreak), .out(priority_encoder_2_out), .en_in(1'b1));  // open: gs, en_out
  and and_1 (and_1_out, ma_dmemAddr[0], comparator_1_eq);
  and and_2 (and_2_out, nor_1_out, comparator_2_eq);
  and and_3 (and_3_out, ma_dmemAddr[0], or_1_out);
  and and_4 (and_4_out, nor_2_out, comparator_5_eq);
  or or_2 (or_2_out, and_1_out, and_2_out);
  and and_5 (and_5_out, or_2_out, ma_mem_write);
  and and_6 (and_6_out, ma_mem_read, or_3_out);
  or or_3 (or_3_out, and_3_out, and_4_out);
  Multiplexer #(.select(3), .width(4)) multiplexer_1 (
    .in0(4'b0000), .in1(4'b0000), .in2(4'b0000), .in3(4'b0110), .in4(4'b0100), .in5(4'b1011), .in6(4'b0010),
    .in7(4'b0011), .out(trap_mcause[3:0]));  // open: sel
  Multiplexer #(.select(3), .width(32)) multiplexer_2 (
    .in0({32{1'b0}}), .in1({32{1'b0}}), .in2({32{1'b0}}), .in3({32{1'b0}}), .in4(ma_dmemAddr),
    .in5(ma_dmemAddr), .in6(ma_instr), .in7(ma_pc), .out(trap_mtval));  // open: sel
  or or_4 (trap_en, and_5_out, and_6_out, ma_is_ecall, ma_is_ebreak, ma_is_illegal);

  assign mret_en = ma_is_mret;
  assign trap_mcause[31:4] = {28{1'b0}};
  assign trap_mepc = ma_pc;

  // Notes on the sheet:
  //   store_misalign
  //   load_misalign
endmodule

module phantom_core (
  input  [31:0] imem_data_a,
  input  [31:0] imem_data_b,
  input  clk,
  input  resetn,
  input  [31:0] dmem_rdata,
  output [31:0] imem_addr_a,
  output [31:0] imem_addr_b,
  output [31:0] dmem_raddr,
  output [31:0] dmem_waddr,
  output [31:0] dmem_wdata,
  output dmem_we,
  output [3:0] dmem_be
);

  wire undriven;

  if_preif_interstage if_preif_interstage_1 (.clk(undriven));  // open: bhr_mux, nextpc, o_blank_o, bhr, prepc
  branch_target_buffer branch_target_buffer_1 ();  // open: next_pc, update_en, clk, update_target, update_idx, btb_rdata
  pattern_history_table pattern_history_table_1 ();  // open: clk, r_bhr, pre_pc, update_en, update_idx, update_taken, update_old, pht_mar, pht_rdata
  preif_if_interstage preif_if_interstage_1 (.clk(undriven));  // open: btb_rdata, pred_taken, nextpc, nextpc_2, o_blank_o, predpc, predpc2, predTaken, pc, pc2, pc4, pc6
  if_id_interstage if_id_interstage_1 (.clk(undriven));  // open: if_predpc, if_predTaken, if_pht_mar, if_pht_rdata, if_pc, if_pc2, if_pc4, if_isComp, if_rs1Index, if_rs2Index, if_rdIndex, if_imm, if_imm2, if_instr, if_isLoad, o_blank_o, predpc, predTaken, phtIdx, phtOld, pc, pc2, pc4, isComp, rs1Index, rs2Index, rdIndex, imm, imm2, instr, isLoad
  id_ex_interstage id_ex_interstage_1 (.clk(undriven));  // open: id_isBranch, id_isJump, id_predpc, id_predTaken, id_phtIdx, id_phtOld, id_pc, id_pc2, id_pc4, id_isComp, id_rs1Index, id_rs2Index, id_rdIndex, id_imm, id_imm2, id_instr, id_aluOp, id_branchType, id_isJalr, id_memRead, id_memWrite, id_memWidth, id_csrEnable, id_csrOp, id_csrUseImm, id_csrIndex, id_isECALL, id_isEBREAK, id_isMRET, id_isIllegal, id_regWrite, id_wbSel, id_rs1Data, id_rs2Data, o_blank_o, isBranch, isJump, predpc, predTaken, phtIdx, phtOld, pc, pc2, pc4, isComp, rs1Index, rs2Index, rdIndex, imm, imm2, instr, aluOp, branchType, isJalr, memRead, memWrite, memWidth, csrEnable, csrOp, csrUseImm, csrIndex, isECALL, isEBREAK, isMRET, isIllegal, regWrite, wbSel, rs1Data, rs2Data
endmodule

module preif_if_interstage (
  input  clk,
  input  [31:0] btb_rdata,
  input  pred_taken,
  input  [31:0] nextpc,
  input  [31:0] nextpc_2,
  output o_blank_o,
  output [31:0] predpc,
  output [31:0] predpc2,
  output predTaken,
  output [31:0] pc,
  output [31:0] pc2,
  output [31:0] pc4,
  output [31:0] pc6
);

  wire [31:0] adder_1_out, adder_2_out, adder_3_out;

  Adder #(.width(32)) adder_1 (.a(btb_rdata), .b(32'h2), .out(adder_1_out), .cin(1'b0));  // open: cout
  Adder #(.width(32)) adder_2 (.a(pc2), .b(32'h2), .out(adder_2_out), .cin(1'b0));  // open: cout
  Adder #(.width(32)) adder_3 (.a(pc2), .b(32'h4), .out(adder_3_out), .cin(1'b0));  // open: cout
  Register #(.width(32)) r_predpc (.D(btb_rdata), .en(clk), .clk(clk), .Q(predpc), .clr(1'b0));
  Register #(.width(32)) r_predpc2 (.D(adder_1_out), .en(clk), .clk(clk), .Q(predpc2), .clr(1'b0));
  Register #(.width(1)) r_predTaken (.D(pred_taken), .en(clk), .clk(clk), .Q(predTaken), .clr(1'b0));
  Register #(.width(32)) r_pc (.D(nextpc), .en(clk), .clk(clk), .Q(pc), .clr(1'b0));
  Register #(.width(32)) r_pc2 (.D(nextpc_2), .en(clk), .clk(clk), .Q(pc2), .clr(1'b0));
  Register #(.width(32)) r_pc4 (.D(adder_2_out), .en(clk), .clk(clk), .Q(pc4), .clr(1'b0));
  Register #(.width(32)) r_pc6 (.D(adder_3_out), .en(clk), .clk(clk), .Q(pc6), .clr(1'b0));

  assign o_blank_o = 1'b0;
endmodule

module if_preif_interstage (
  input  clk,
  input  [12:0] bhr_mux,
  input  [31:0] nextpc,
  output o_blank_o,
  output [12:0] bhr,
  output [31:0] prepc
);

  Register #(.width(13)) r_bhr (.D(bhr_mux), .en(clk), .clk(clk), .Q(bhr), .clr(1'b0));
  Register #(.width(32)) r_prepc (.D(nextpc), .en(clk), .clk(clk), .Q(prepc), .clr(1'b0));

  assign o_blank_o = 1'b0;
endmodule

module if_id_interstage (
  input  clk,
  input  [31:0] if_predpc,
  input  if_predTaken,
  input  [12:0] if_pht_mar,
  input  [1:0] if_pht_rdata,
  input  [31:0] if_pc,
  input  [31:0] if_pc2,
  input  [31:0] if_pc4,
  input  if_isComp,
  input  [4:0] if_rs1Index,
  input  [4:0] if_rs2Index,
  input  [4:0] if_rdIndex,
  input  [31:0] if_imm,
  input  [31:0] if_imm2,
  input  [31:0] if_instr,
  input  if_isLoad,
  output o_blank_o,
  output [31:0] predpc,
  output predTaken,
  output [12:0] phtIdx,
  output [1:0] phtOld,
  output [31:0] pc,
  output [31:0] pc2,
  output [31:0] pc4,
  output isComp,
  output [4:0] rs1Index,
  output [4:0] rs2Index,
  output [4:0] rdIndex,
  output [31:0] imm,
  output [31:0] imm2,
  output [31:0] instr,
  output isLoad
);

  Register #(.width(32)) r_predpc (.D(if_predpc), .en(clk), .clk(clk), .Q(predpc), .clr(1'b0));
  Register #(.width(1)) r_predTaken (.D(if_predTaken), .en(clk), .clk(clk), .Q(predTaken), .clr(1'b0));
  Register #(.width(13)) r_phtIdx (.D(if_pht_mar), .en(clk), .clk(clk), .Q(phtIdx), .clr(1'b0));
  Register #(.width(2)) r_phtOld (.D(if_pht_rdata), .en(clk), .clk(clk), .Q(phtOld), .clr(1'b0));
  Register #(.width(32)) r_pc (.D(if_pc), .en(clk), .clk(clk), .Q(pc), .clr(1'b0));
  Register #(.width(32)) r_pc2 (.D(if_pc2), .en(clk), .clk(clk), .Q(pc2), .clr(1'b0));
  Register #(.width(32)) r_pc4 (.D(if_pc4), .en(clk), .clk(clk), .Q(pc4), .clr(1'b0));
  Register #(.width(1)) r_isComp (.D(if_isComp), .en(clk), .clk(clk), .Q(isComp), .clr(1'b0));
  Register #(.width(5)) r_rs1Index (.D(if_rs1Index), .en(clk), .clk(clk), .Q(rs1Index), .clr(1'b0));
  Register #(.width(5)) r_rs2Index (.D(if_rs2Index), .en(clk), .clk(clk), .Q(rs2Index), .clr(1'b0));
  Register #(.width(5)) r_rdIndex (.D(if_rdIndex), .en(clk), .clk(clk), .Q(rdIndex), .clr(1'b0));
  Register #(.width(32)) r_imm (.D(if_imm), .en(clk), .clk(clk), .Q(imm), .clr(1'b0));
  Register #(.width(32)) r_imm2 (.D(if_imm2), .en(clk), .clk(clk), .Q(imm2), .clr(1'b0));
  Register #(.width(32)) r_instr (.D(if_instr), .en(clk), .clk(clk), .Q(instr), .clr(1'b0));
  Register #(.width(1)) r_isLoad (.D(if_isLoad), .en(clk), .clk(clk), .Q(isLoad), .clr(1'b0));

  assign o_blank_o = 1'b0;
endmodule

module id_ex_interstage (
  input  clk,
  input  id_isBranch,
  input  id_isJump,
  input  [31:0] id_predpc,
  input  id_predTaken,
  input  [12:0] id_phtIdx,
  input  [1:0] id_phtOld,
  input  [31:0] id_pc,
  input  [31:0] id_pc2,
  input  [31:0] id_pc4,
  input  id_isComp,
  input  [4:0] id_rs1Index,
  input  [4:0] id_rs2Index,
  input  [4:0] id_rdIndex,
  input  [31:0] id_imm,
  input  [31:0] id_imm2,
  input  [31:0] id_instr,
  input  [3:0] id_aluOp,
  input  [2:0] id_branchType,
  input  id_isJalr,
  input  id_memRead,
  input  id_memWrite,
  input  [2:0] id_memWidth,
  input  id_csrEnable,
  input  [1:0] id_csrOp,
  input  id_csrUseImm,
  input  [11:0] id_csrIndex,
  input  id_isECALL,
  input  id_isEBREAK,
  input  id_isMRET,
  input  id_isIllegal,
  input  id_regWrite,
  input  [1:0] id_wbSel,
  input  [31:0] id_rs1Data,
  input  [31:0] id_rs2Data,
  output o_blank_o,
  output isBranch,
  output isJump,
  output [31:0] predpc,
  output predTaken,
  output [12:0] phtIdx,
  output [1:0] phtOld,
  output [31:0] pc,
  output [31:0] pc2,
  output [31:0] pc4,
  output isComp,
  output [4:0] rs1Index,
  output [4:0] rs2Index,
  output [4:0] rdIndex,
  output [31:0] imm,
  output [31:0] imm2,
  output [31:0] instr,
  output [3:0] aluOp,
  output [2:0] branchType,
  output isJalr,
  output memRead,
  output memWrite,
  output [2:0] memWidth,
  output csrEnable,
  output [1:0] csrOp,
  output csrUseImm,
  output [11:0] csrIndex,
  output isECALL,
  output isEBREAK,
  output isMRET,
  output isIllegal,
  output regWrite,
  output [1:0] wbSel,
  output [31:0] rs1Data,
  output [31:0] rs2Data
);

  Register #(.width(1)) r_isBranch (.D(id_isBranch), .en(clk), .clk(clk), .Q(isBranch), .clr(1'b0));
  Register #(.width(1)) r_isJump (.D(id_isJump), .en(clk), .clk(clk), .Q(isJump), .clr(1'b0));
  Register #(.width(32)) r_predpc (.D(id_predpc), .en(clk), .clk(clk), .Q(predpc), .clr(1'b0));
  Register #(.width(1)) r_predTaken (.D(id_predTaken), .en(clk), .clk(clk), .Q(predTaken), .clr(1'b0));
  Register #(.width(13)) r_phtIdx (.D(id_phtIdx), .en(clk), .clk(clk), .Q(phtIdx), .clr(1'b0));
  Register #(.width(2)) r_phtOld (.D(id_phtOld), .en(clk), .clk(clk), .Q(phtOld), .clr(1'b0));
  Register #(.width(32)) r_pc (.D(id_pc), .en(clk), .clk(clk), .Q(pc), .clr(1'b0));
  Register #(.width(32)) r_pc2 (.D(id_pc2), .en(clk), .clk(clk), .Q(pc2), .clr(1'b0));
  Register #(.width(32)) r_pc4 (.D(id_pc4), .en(clk), .clk(clk), .Q(pc4), .clr(1'b0));
  Register #(.width(1)) r_isComp (.D(id_isComp), .en(clk), .clk(clk), .Q(isComp), .clr(1'b0));
  Register #(.width(5)) r_rs1Index (.D(id_rs1Index), .en(clk), .clk(clk), .Q(rs1Index), .clr(1'b0));
  Register #(.width(5)) r_rs2Index (.D(id_rs2Index), .en(clk), .clk(clk), .Q(rs2Index), .clr(1'b0));
  Register #(.width(5)) r_rdIndex (.D(id_rdIndex), .en(clk), .clk(clk), .Q(rdIndex), .clr(1'b0));
  Register #(.width(32)) r_imm (.D(id_imm), .en(clk), .clk(clk), .Q(imm), .clr(1'b0));
  Register #(.width(32)) r_imm2 (.D(id_imm2), .en(clk), .clk(clk), .Q(imm2), .clr(1'b0));
  Register #(.width(32)) r_instr (.D(id_instr), .en(clk), .clk(clk), .Q(instr), .clr(1'b0));
  Register #(.width(4)) r_aluOp (.D(id_aluOp), .en(clk), .clk(clk), .Q(aluOp), .clr(1'b0));
  Register #(.width(3)) r_branchType (.D(id_branchType), .en(clk), .clk(clk), .Q(branchType), .clr(1'b0));
  Register #(.width(1)) r_isJalr (.D(id_isJalr), .en(clk), .clk(clk), .Q(isJalr), .clr(1'b0));
  Register #(.width(1)) r_memRead (.D(id_memRead), .en(clk), .clk(clk), .Q(memRead), .clr(1'b0));
  Register #(.width(1)) r_memWrite (.D(id_memWrite), .en(clk), .clk(clk), .Q(memWrite), .clr(1'b0));
  Register #(.width(3)) r_memWidth (.D(id_memWidth), .en(clk), .clk(clk), .Q(memWidth), .clr(1'b0));
  Register #(.width(1)) r_csrEnable (.D(id_csrEnable), .en(clk), .clk(clk), .Q(csrEnable), .clr(1'b0));
  Register #(.width(2)) r_csrOp (.D(id_csrOp), .en(clk), .clk(clk), .Q(csrOp), .clr(1'b0));
  Register #(.width(1)) r_csrUseImm (.D(id_csrUseImm), .en(clk), .clk(clk), .Q(csrUseImm), .clr(1'b0));
  Register #(.width(12)) r_csrIndex (.D(id_csrIndex), .en(clk), .clk(clk), .Q(csrIndex), .clr(1'b0));
  Register #(.width(1)) r_isECALL (.D(id_isECALL), .en(clk), .clk(clk), .Q(isECALL), .clr(1'b0));
  Register #(.width(1)) r_isEBREAK (.D(id_isEBREAK), .en(clk), .clk(clk), .Q(isEBREAK), .clr(1'b0));
  Register #(.width(1)) r_isMRET (.D(id_isMRET), .en(clk), .clk(clk), .Q(isMRET), .clr(1'b0));
  Register #(.width(1)) r_isIllegal (.D(id_isIllegal), .en(clk), .clk(clk), .Q(isIllegal), .clr(1'b0));
  Register #(.width(1)) r_regWrite (.D(id_regWrite), .en(clk), .clk(clk), .Q(regWrite), .clr(1'b0));
  Register #(.width(2)) r_wbSel (.D(id_wbSel), .en(clk), .clk(clk), .Q(wbSel), .clr(1'b0));
  Register #(.width(32)) r_rs1Data (.D(id_rs1Data), .en(clk), .clk(clk), .Q(rs1Data), .clr(1'b0));
  Register #(.width(32)) r_rs2Data (.D(id_rs2Data), .en(clk), .clk(clk), .Q(rs2Data), .clr(1'b0));

  assign o_blank_o = 1'b0;
endmodule

module ex_ma_interstage (
  input  clk,
  input  ex_isBranch,
  input  ex_isJump,
  input  [31:0] ex_predpc,
  input  ex_predTaken,
  input  [12:0] ex_phtIdx,
  input  [1:0] ex_phtOld,
  input  [31:0] ex_pc,
  input  [31:0] ex_pc2,
  input  [31:0] ex_pc4,
  input  ex_isComp,
  input  [31:0] ex_rs1Fwd,
  input  [31:0] ex_rs2Fwd,
  input  [4:0] ex_rdIndex,
  input  ex_rdNonZero,
  input  ex_csrWrGuard,
  input  [31:0] ex_instr,
  input  [31:0] ex_aluResult,
  input  [31:0] ex_dmemAddr,
  input  ex_memRead,
  input  ex_memWrite,
  input  [2:0] ex_memWidth,
  input  ex_csrEnable,
  input  [1:0] ex_csrOp,
  input  ex_csrUseImm,
  input  [11:0] ex_csrIndex,
  input  ex_isECALL,
  input  ex_isEBREAK,
  input  ex_isMRET,
  input  ex_isIllegal,
  input  ex_regWrite,
  input  [1:0] ex_wbSel,
  output o_blank_o,
  output isBranch,
  output isJump,
  output [31:0] predpc,
  output predTaken,
  output [12:0] phtIdx,
  output [1:0] phtOld,
  output [31:0] pc,
  output [31:0] pc2,
  output [31:0] pc4,
  output isComp,
  output [31:0] rs1Fwd,
  output [31:0] rs2Fwd,
  output [4:0] rdIndex,
  output rdNonZero,
  output csrWrGuard,
  output [31:0] instr,
  output [31:0] aluResult,
  output [31:0] dmemAddr,
  output memRead,
  output memWrite,
  output [2:0] memWidth,
  output csrEnable,
  output [1:0] csrOp,
  output csrUseImm,
  output [11:0] csrIndex,
  output isECALL,
  output isEBREAK,
  output isMRET,
  output isIllegal,
  output regWrite,
  output [1:0] wbSel
);

  Register #(.width(1)) r_isBranch (.D(ex_isBranch), .en(clk), .clk(clk), .Q(isBranch), .clr(1'b0));
  Register #(.width(1)) r_isJump (.D(ex_isJump), .en(clk), .clk(clk), .Q(isJump), .clr(1'b0));
  Register #(.width(32)) r_predpc (.D(ex_predpc), .en(clk), .clk(clk), .Q(predpc), .clr(1'b0));
  Register #(.width(1)) r_predTaken (.D(ex_predTaken), .en(clk), .clk(clk), .Q(predTaken), .clr(1'b0));
  Register #(.width(13)) r_phtIdx (.D(ex_phtIdx), .en(clk), .clk(clk), .Q(phtIdx), .clr(1'b0));
  Register #(.width(2)) r_phtOld (.D(ex_phtOld), .en(clk), .clk(clk), .Q(phtOld), .clr(1'b0));
  Register #(.width(32)) r_pc (.D(ex_pc), .en(clk), .clk(clk), .Q(pc), .clr(1'b0));
  Register #(.width(32)) r_pc2 (.D(ex_pc2), .en(clk), .clk(clk), .Q(pc2), .clr(1'b0));
  Register #(.width(32)) r_pc4 (.D(ex_pc4), .en(clk), .clk(clk), .Q(pc4), .clr(1'b0));
  Register #(.width(1)) r_isComp (.D(ex_isComp), .en(clk), .clk(clk), .Q(isComp), .clr(1'b0));
  Register #(.width(32)) r_rs1Fwd (.D(ex_rs1Fwd), .en(clk), .clk(clk), .Q(rs1Fwd), .clr(1'b0));
  Register #(.width(32)) r_rs2Fwd (.D(ex_rs2Fwd), .en(clk), .clk(clk), .Q(rs2Fwd), .clr(1'b0));
  Register #(.width(5)) r_rdIndex (.D(ex_rdIndex), .en(clk), .clk(clk), .Q(rdIndex), .clr(1'b0));
  Register #(.width(1)) r_rdNonZero (.D(ex_rdNonZero), .en(clk), .clk(clk), .Q(rdNonZero), .clr(1'b0));
  Register #(.width(1)) r_csrWrGuard (.D(ex_csrWrGuard), .en(clk), .clk(clk), .Q(csrWrGuard), .clr(1'b0));
  Register #(.width(32)) r_instr (.D(ex_instr), .en(clk), .clk(clk), .Q(instr), .clr(1'b0));
  Register #(.width(32)) r_aluResult (.D(ex_aluResult), .en(clk), .clk(clk), .Q(aluResult), .clr(1'b0));
  Register #(.width(32)) r_dmemAddr (.D(ex_dmemAddr), .en(clk), .clk(clk), .Q(dmemAddr), .clr(1'b0));
  Register #(.width(1)) r_memRead (.D(ex_memRead), .en(clk), .clk(clk), .Q(memRead), .clr(1'b0));
  Register #(.width(1)) r_memWrite (.D(ex_memWrite), .en(clk), .clk(clk), .Q(memWrite), .clr(1'b0));
  Register #(.width(3)) r_memWidth (.D(ex_memWidth), .en(clk), .clk(clk), .Q(memWidth), .clr(1'b0));
  Register #(.width(1)) r_csrEnable (.D(ex_csrEnable), .en(clk), .clk(clk), .Q(csrEnable), .clr(1'b0));
  Register #(.width(2)) r_csrOp (.D(ex_csrOp), .en(clk), .clk(clk), .Q(csrOp), .clr(1'b0));
  Register #(.width(1)) r_csrUseImm (.D(ex_csrUseImm), .en(clk), .clk(clk), .Q(csrUseImm), .clr(1'b0));
  Register #(.width(12)) r_csrIndex (.D(ex_csrIndex), .en(clk), .clk(clk), .Q(csrIndex), .clr(1'b0));
  Register #(.width(1)) r_isECALL (.D(ex_isECALL), .en(clk), .clk(clk), .Q(isECALL), .clr(1'b0));
  Register #(.width(1)) r_isEBREAK (.D(ex_isEBREAK), .en(clk), .clk(clk), .Q(isEBREAK), .clr(1'b0));
  Register #(.width(1)) r_isMRET (.D(ex_isMRET), .en(clk), .clk(clk), .Q(isMRET), .clr(1'b0));
  Register #(.width(1)) r_isIllegal (.D(ex_isIllegal), .en(clk), .clk(clk), .Q(isIllegal), .clr(1'b0));
  Register #(.width(1)) r_regWrite (.D(ex_regWrite), .en(clk), .clk(clk), .Q(regWrite), .clr(1'b0));
  Register #(.width(2)) r_wbSel (.D(ex_wbSel), .en(clk), .clk(clk), .Q(wbSel), .clr(1'b0));

  assign o_blank_o = 1'b0;
endmodule
